# Fritzing sketch TM1638-RPi3 (saved by Fritzing 0.9.2b)

parts:
  Raspberry_Pi_1 = Raspberry Pi 3 [part_number=RPI-3-V1.2]
  TM1638_Led_and_Key1 = TM1638_Led_and_Key [package=THT]

nets:
  3V3: Raspberry_Pi_1.3v3, Raspberry_Pi_1.GPIO2, Raspberry_Pi_1.GIPO22, Raspberry_Pi_1.3V3, TM1638_Led_and_Key1.VCC, TM1638_Led_and_Key1.STB
  N1: Raspberry_Pi_1.GIPO17, TM1638_Led_and_Key1.DIO
  N2: Raspberry_Pi_1.GIPO27, TM1638_Led_and_Key1.CLK
  GND: Raspberry_Pi_1.GIPO14, Raspberry_Pi_1.GND, TM1638_Led_and_Key1.GND
